# Fritzing sketch RelogioBCD (saved by Fritzing 0.9.3b)
circuit board: 8.46667cm x 5.64444cm

parts:
  U1 = ESP-12F (ESP8266 WiFi Module) [part_number=ESP8266]
  R1 = Resistor [tolerance=±5% resistance=150 package=THT]
  R2 = Resistor [tolerance=±5% resistance=150 package=THT]
  R3 = Resistor [tolerance=±5% resistance=150 package=THT]
  R4 = Resistor [tolerance=±5% resistance=150 package=THT]
  R5 = Resistor [tolerance=±5% resistance=150 package=THT]
  R6 = Resistor [tolerance=±5% resistance=150 package=THT]
  R7 = Resistor [tolerance=±5% resistance=150 package=THT]
  R8 = Resistor [tolerance=±5% resistance=150 package=THT]
  Disp1 = LBT2088AH [part_number=LBT2088AH]

nets:
  N1: U1.RXD0, Disp1.pin2
  N2: U1.GPIO0, R2.Pin_0
  N3: U1.GPIO2, Disp1.pin_7
  N4: U1.TXD0, Disp1.pin1
  N5: U1.GPIO15, R3.Pin_0
  N6: U1.GPIO4, Disp1.pin_5
  N7: U1.GPIO5, R1.Pin_0
  N8: U1.GPIO16, R4.Pin_1
  N9: U1.GPIO14, Disp1.pin_14
  N10: U1.GPIO12, R5.Pin_1
  N11: U1.GPIO13, Disp1.pin_12
  N12: U1.SCLK, Disp1.pin_8
  N13: U1.MOSI, R8.Pin_1
  N14: U1.GPIO10, Disp1.pin_9
  N15: U1.GPIO9, R6.Pin_1
  N16: U1.CS0, R7.Pin_1
  N17: R1.Pin_1, Disp1.pin_3
  N18: R2.Pin_1, Disp1.pin_4
  N19: R3.Pin_1, Disp1.pin_6
  N20: R4.Pin_0, Disp1.pin_16
  N21: R5.Pin_0, Disp1.pin_15
  N22: R6.Pin_0, Disp1.pin_11
  N23: R7.Pin_0, Disp1.pin_13
  N24: R8.Pin_0, Disp1.pin_10

custom parts:
  ESP-12F (ESP8266 WiFi Module): WiFi Module based on the ESP8266 with onboard PCB antenna and UART communications
